// Logisim project CPU.circ as structural Verilog: 2 circuits, main circuit ULA
module ULA (
  input  [15:0] A,
  input  [15:0] B,
  input  [3:0] op,
  output [15:0] out_4
);

  Adder #(.width(16)) adder_1 (.a(A), .b(B), .out(out_4));  // open: cin, cout
  Multiplier #(.width(16)) multiplier_1 ();  // open: a, b, out, cin, cout
  Subtractor #(.width(16)) subtractor_1 ();  // open: a, b, out, bin, bout
  Divider divider_1 ();  // open: a, b, out, upper, rem
  Comparator comparator_1 ();  // open: a, b, gt, eq, lt

  // Other names for the same wires on the sheet: Output[15:0] = out_4
endmodule

module Soma (
  input  in_1,
  input  in_2,
  output out_3,
  output out_4
);

  xor xor_1 (out_3, in_1, in_2);
  and and_1 (out_4, in_1, in_2);
endmodule
